// Logisim project PROJECTARCH.circ as structural Verilog: 14 circuits, main circuit Final Datapath
module Final_Datapath (
);

  wire alu_1_jr, alu_1_zero, alu_control_1_lws, CLK, control_unit_1_alusrc, control_unit_1_beq,
       control_unit_1_extop, control_unit_1_jal, control_unit_1_jump, control_unit_1_lbu,
       control_unit_1_membyte, control_unit_1_memread, control_unit_1_memtoreg, control_unit_1_memwrite,
       control_unit_1_r_type, control_unit_1_regdest, control_unit_1_regwrite, ex_buffer_1_out_14,
       ex_buffer_1_out_15, ex_buffer_1_out_16, ex_buffer_1_out_17, ex_buffer_1_out_18, id_buffer_1_out_33,
       id_buffer_1_out_34, id_buffer_1_out_35, id_buffer_1_out_36, id_buffer_1_out_37, id_buffer_1_out_38,
       id_buffer_1_out_39, id_buffer_1_out_40, id_buffer_1_out_41, id_buffer_1_out_42, id_buffer_1_out_43,
       JAL, mem_buffer_1_out_10, or_1_out, or_2_out, regWrite_mem, regWrite_WB;
  wire [1:0] forward_1_forwarda, forward_1_forwardb, pc_control_1_pc;
  wire [2:0] alu_control_1_alu_control, control_unit_1_aluop, ex_buffer_1_out_11, id_buffer_1_out_24,
       id_buffer_1_out_25, id_buffer_1_out_26, id_buffer_1_out_31, multiplexer_2_out, multiplexer_3_out,
       multiplexer_5_out, RW;
  wire [5:0] id_buffer_1_out_28;
  wire [15:0] adder_1_out, adder_2_out, adder_3_out, bit_extender_1_out, bit_extender_2_out,
       byte_extender_1_out, ex_buffer_1_out_12, ex_buffer_1_out_13, extender_1_out, id_buffer_1_out_23,
       id_buffer_1_out_27, id_buffer_1_out_29, id_buffer_1_out_30, if_buffer_1_ir_out, if_buffer_1_pc_out,
       JR, mem_buffer_1_out_8, mem_buffer_1_out_9, multiplexer_1_out, multiplexer_4_out, multiplexer_6_out,
       multiplexer_7_out, multiplexer_8_out, multiplexer_9_out, multiplexer_10_out, multiplexer_11_out, PC_q,
       ram_1_data, ram_2_data, register_file_1_bus_a, register_file_1_bus_b;

  Register #(.width(16)) PC (.D(multiplexer_1_out), .Q(PC_q), .clk(CLK));  // open: en, clr
  Multiplexer #(.select(2), .width(16), .enable("false")) multiplexer_1 (
    .in0(adder_1_out), .in1(id_buffer_1_out_23), .in2(adder_3_out), .in3(JR), .out(multiplexer_1_out),
    .sel(pc_control_1_pc));
  Clock clock_1 (.out(CLK));
  Adder #(.width(16)) adder_1 (.a(PC_q), .b(16'h1), .out(adder_1_out));  // open: cin, cout
  RAM #(.addrWidth(16), .dataWidth(16)) ram_1 (
    .addr(PC_q), .data(ram_1_data), .sel(1'b1), .ld(1'b1));  // open: clk, clr
  IF_buffer if_buffer_1 (
    .PC_iin(adder_1_out), .IR_in(ram_1_data), .CLK(CLK), .PC_out(if_buffer_1_pc_out),
    .IR_out(if_buffer_1_ir_out));
  assign bit_extender_1_out = {{4{if_buffer_1_ir_out[11]}}, if_buffer_1_ir_out[11:0]};  // Bit_Extender bit_extender_1
  Control_Unit control_unit_1 (
    .Opcode(if_buffer_1_ir_out[15:12]), .Jump(control_unit_1_jump), .RegDest(control_unit_1_regdest),
    .BEQ(control_unit_1_beq), .MemWrite(control_unit_1_memwrite), .MemRead(control_unit_1_memread),
    .MemToReg(control_unit_1_memtoreg), .RegWrite(control_unit_1_regwrite), .ALUSrc(control_unit_1_alusrc),
    .ExtOp(control_unit_1_extop), .R_Type(control_unit_1_r_type), .ALUOp(control_unit_1_aluop),
    .MemByte(control_unit_1_membyte), .lbu(control_unit_1_lbu), .Jal(control_unit_1_jal));
  Adder #(.width(16)) adder_2 (.a(bit_extender_1_out), .b(if_buffer_1_pc_out), .out(adder_2_out));  // open: cin, cout
  Multiplexer #(.width(3), .enable("false")) multiplexer_2 (
    .in0(multiplexer_3_out), .in1(3'b111), .out(multiplexer_2_out), .sel(JAL));
  Multiplexer #(.width(3), .enable("false")) multiplexer_3 (
    .in0(if_buffer_1_ir_out[8:6]), .in1(RW), .out(multiplexer_3_out), .sel(control_unit_1_regdest));
  Register_File register_file_1 (
    .RW(multiplexer_2_out), .RegWrite(control_unit_1_regwrite), .CLK(CLK), .Bus_W(multiplexer_4_out),
    .RA(if_buffer_1_ir_out[11:9]), .Bus_B(register_file_1_bus_b), .Bus_A(register_file_1_bus_a),
    .RB(if_buffer_1_ir_out[8:6]));
  Alu_Control alu_control_1 (
    .Main_Control(control_unit_1_aluop), .Function(if_buffer_1_ir_out[2:0]), .Type(control_unit_1_r_type),
    .ALU_Control(alu_control_1_alu_control), .Lws(alu_control_1_lws));
  or or_1 (or_1_out, control_unit_1_memtoreg, alu_control_1_lws, control_unit_1_memread);
  ID_buffer id_buffer_1 (
    .in_5(if_buffer_1_pc_out), .in_6(if_buffer_1_ir_out[5:0]), .in_7(register_file_1_bus_a),
    .in_8(register_file_1_bus_b), .in_9(alu_control_1_alu_control), .in_11(control_unit_1_jump),
    .in_15(control_unit_1_beq), .in_16(control_unit_1_memwrite), .in_17(or_1_out), .in_18(or_1_out),
    .in_20(control_unit_1_alusrc), .in_21(control_unit_1_extop), .out_27(id_buffer_1_out_27),
    .out_28(id_buffer_1_out_28), .out_29(id_buffer_1_out_29), .out_30(id_buffer_1_out_30),
    .out_31(id_buffer_1_out_31), .out_33(id_buffer_1_out_33), .out_37(id_buffer_1_out_37),
    .out_38(id_buffer_1_out_38), .out_39(id_buffer_1_out_39), .out_40(id_buffer_1_out_40),
    .out_42(id_buffer_1_out_42), .out_43(id_buffer_1_out_43), .CLK(CLK), .in_4(if_buffer_1_ir_out[5:3]),
    .out_26(id_buffer_1_out_26), .in_3(if_buffer_1_ir_out[8:6]), .out_25(id_buffer_1_out_25),
    .in_2(if_buffer_1_ir_out[11:9]), .out_24(id_buffer_1_out_24), .in_14(control_unit_1_regdest),
    .out_36(id_buffer_1_out_36), .in_19(control_unit_1_regwrite), .out_41(id_buffer_1_out_41),
    .in_12(control_unit_1_membyte), .out_34(id_buffer_1_out_34), .in_13(control_unit_1_lbu),
    .out_35(id_buffer_1_out_35), .in_1(adder_2_out), .out_23(id_buffer_1_out_23), .in_10(control_unit_1_jal),
    .out_32(JAL));
  Multiplexer #(.width(16), .enable("false")) multiplexer_4 (
    .in0(multiplexer_11_out), .in1(id_buffer_1_out_27), .out(multiplexer_4_out), .sel(JAL));
  Extender extender_1 (.Imm(id_buffer_1_out_28), .Out(extender_1_out), .ExtOp(id_buffer_1_out_43));
  Adder #(.width(16)) adder_3 (.a(id_buffer_1_out_27), .b(extender_1_out), .out(adder_3_out));  // open: cin, cout
  Multiplexer #(.width(3), .enable("false")) multiplexer_5 (
    .in0(id_buffer_1_out_25), .in1(id_buffer_1_out_26), .out(multiplexer_5_out), .sel(id_buffer_1_out_36));
  Multiplexer #(.select(2), .width(16), .enable("false")) multiplexer_6 (
    .in0(id_buffer_1_out_29), .in1(multiplexer_11_out), .in2(ex_buffer_1_out_12), .out(multiplexer_6_out),
    .sel(forward_1_forwarda));  // open: in3
  Multiplexer #(.select(2), .width(16), .enable("false")) multiplexer_7 (
    .in0(id_buffer_1_out_30), .in1(multiplexer_11_out), .in2(ex_buffer_1_out_12), .out(multiplexer_7_out),
    .sel(forward_1_forwardb));  // open: in3
  Multiplexer #(.width(16), .enable("false")) multiplexer_8 (
    .in0(multiplexer_7_out), .in1(extender_1_out), .out(multiplexer_8_out), .sel(id_buffer_1_out_42));
  Forward forward_1 (
    .RS(id_buffer_1_out_24), .RT(id_buffer_1_out_25), .Rd_mem(ex_buffer_1_out_11), .Rd_wb(RW),
    .RegWrite_mem(regWrite_mem), .RegWrite_WB(regWrite_WB), .ForwardA(forward_1_forwarda),
    .ForwardB(forward_1_forwardb));
  PC_Control pc_control_1 (
    .Jump(id_buffer_1_out_33), .BEQ(id_buffer_1_out_37), .PC(pc_control_1_pc), .Zero(alu_1_zero),
    .JR(alu_1_jr), .Rs(id_buffer_1_out_24));
  ALU alu_1 (
    .A(multiplexer_6_out), .B(multiplexer_8_out), .Result(JR), .Zero(alu_1_zero),
    .ALU_Control(id_buffer_1_out_31), .JR(alu_1_jr));
  EX_buffer ex_buffer_1 (
    .in_1(multiplexer_5_out), .out_11(ex_buffer_1_out_11), .in_2(JR), .out_12(ex_buffer_1_out_12),
    .in_3(multiplexer_7_out), .out_13(ex_buffer_1_out_13), .in_6(id_buffer_1_out_38),
    .out_16(ex_buffer_1_out_16), .in_7(id_buffer_1_out_39), .out_17(ex_buffer_1_out_17),
    .in_8(id_buffer_1_out_40), .out_18(ex_buffer_1_out_18), .CLK(CLK), .in_9(id_buffer_1_out_41),
    .out_19(regWrite_mem), .in_4(id_buffer_1_out_34), .out_14(ex_buffer_1_out_14), .in_5(id_buffer_1_out_35),
    .out_15(ex_buffer_1_out_15));
  Multiplexer #(.width(16), .enable("false")) multiplexer_9 (
    .in0(ex_buffer_1_out_13), .in1(bit_extender_2_out), .out(multiplexer_9_out), .sel(ex_buffer_1_out_14));
  or or_2 (or_2_out, ex_buffer_1_out_16, ex_buffer_1_out_17);
  assign bit_extender_2_out = {{8{ex_buffer_1_out_13[7]}}, ex_buffer_1_out_13[7:0]};  // Bit_Extender bit_extender_2
  RAM #(.addrWidth(16), .dataWidth(16), .bus("separate")) ram_2 (
    .addr(ex_buffer_1_out_12), .din(multiplexer_9_out), .data(ram_2_data), .str(ex_buffer_1_out_16),
    .sel(or_2_out), .clk(CLK), .ld(ex_buffer_1_out_17), .clr(1'b0));
  byte_Extender byte_extender_1 (.Imm(ram_2_data), .Out(byte_extender_1_out), .lbu(ex_buffer_1_out_15));
  Multiplexer #(.width(16), .enable("false")) multiplexer_10 (
    .in0(ram_2_data), .in1(byte_extender_1_out), .out(multiplexer_10_out), .sel(ex_buffer_1_out_14));
  MEM_buffer mem_buffer_1 (
    .in_1(ex_buffer_1_out_11), .in_2(ex_buffer_1_out_12), .in_3(multiplexer_10_out),
    .in_4(ex_buffer_1_out_18), .out_7(RW), .out_8(mem_buffer_1_out_8), .out_9(mem_buffer_1_out_9),
    .out_10(mem_buffer_1_out_10), .CLK(CLK), .in_5(regWrite_mem), .out_11(regWrite_WB));
  Multiplexer #(.width(16), .enable("false")) multiplexer_11 (
    .in0(mem_buffer_1_out_8), .in1(mem_buffer_1_out_9), .out(multiplexer_11_out), .sel(mem_buffer_1_out_10));

  // Notes on the sheet:
  //   Stage 1: IF 
  //   Instruction Memory
  //   Stage 2: Decode
  //   Stage 3: Execute
  //   Stage 4: Memory
  //   Stage 5: WD
endmodule

module Register_File (
  input  [15:0] Bus_W,
  input  [2:0] RA,
  input  [2:0] RW,
  input  RegWrite,
  input  [2:0] RB,
  input  CLK,
  output [15:0] Bus_A,
  output [15:0] Bus_B
);

  wire decoder_1_out1, decoder_1_out2, decoder_1_out3, decoder_1_out4, decoder_1_out5, decoder_1_out6,
       decoder_1_out7;
  wire [15:0] Register_1_data_out, Register_2_data_out, Register_3_data_out, Register_4_data_out,
       Register_5_data_out, Register_6_data_out, Register_7_data_out;

  Decoder #(.select(3)) decoder_1 (
    .out1(decoder_1_out1), .out2(decoder_1_out2), .out3(decoder_1_out3), .out4(decoder_1_out4),
    .out5(decoder_1_out5), .out6(decoder_1_out6), .out7(decoder_1_out7), .sel(RW), .en(RegWrite));  // open: out0
  _16_bit_Register Register_1 (.CLK(CLK), .Write(decoder_1_out1), .Data_In(Bus_W), .Data_Out(Register_1_data_out));
  _16_bit_Register Register_2 (.CLK(CLK), .Write(decoder_1_out2), .Data_In(Bus_W), .Data_Out(Register_2_data_out));
  _16_bit_Register Register_3 (.CLK(CLK), .Write(decoder_1_out3), .Data_In(Bus_W), .Data_Out(Register_3_data_out));
  _16_bit_Register Register_4 (.CLK(CLK), .Write(decoder_1_out4), .Data_In(Bus_W), .Data_Out(Register_4_data_out));
  _16_bit_Register Register_5 (.CLK(CLK), .Write(decoder_1_out5), .Data_In(Bus_W), .Data_Out(Register_5_data_out));
  _16_bit_Register Register_6 (.CLK(CLK), .Write(decoder_1_out6), .Data_In(Bus_W), .Data_Out(Register_6_data_out));
  _16_bit_Register Register_7 (.CLK(CLK), .Write(decoder_1_out7), .Data_In(Bus_W), .Data_Out(Register_7_data_out));
  Multiplexer #(.select(3), .width(16), .enable("false")) multiplexer_1 (
    .in0({16{1'b0}}), .in1(Register_1_data_out), .in2(Register_2_data_out), .in3(Register_3_data_out),
    .in4(Register_4_data_out), .in5(Register_5_data_out), .in6(Register_6_data_out),
    .in7(Register_7_data_out), .out(Bus_A), .sel(RA));
  Multiplexer #(.select(3), .width(16), .enable("false")) multiplexer_2 (
    .in0({16{1'b0}}), .in1(Register_1_data_out), .in2(Register_2_data_out), .in3(Register_3_data_out),
    .in4(Register_4_data_out), .in5(Register_5_data_out), .in6(Register_6_data_out),
    .in7(Register_7_data_out), .out(Bus_B), .sel(RB));
endmodule

module _16_bit_Register (
  input  CLK,
  input  Write,
  input  [15:0] Data_In,
  output [15:0] Data_Out
);

  D_Flip_Flop d_ff_1 (.clk(CLK), .D(Data_In[0]), .Q(Data_Out[0]), .en(Write));  // open: Qn, preset, reset
  D_Flip_Flop d_ff_2 (.clk(CLK), .D(Data_In[1]), .Q(Data_Out[1]), .en(Write));  // open: Qn, preset, reset
  D_Flip_Flop d_ff_3 (.clk(CLK), .D(Data_In[2]), .Q(Data_Out[2]), .en(Write));  // open: Qn, preset, reset
  D_Flip_Flop d_ff_4 (.clk(CLK), .D(Data_In[3]), .Q(Data_Out[3]), .en(Write));  // open: Qn, preset, reset
  D_Flip_Flop d_ff_5 (.clk(CLK), .D(Data_In[4]), .Q(Data_Out[4]), .en(Write));  // open: Qn, preset, reset
  D_Flip_Flop d_ff_6 (.clk(CLK), .D(Data_In[5]), .Q(Data_Out[5]), .en(Write));  // open: Qn, preset, reset
  D_Flip_Flop d_ff_7 (.clk(CLK), .D(Data_In[6]), .Q(Data_Out[6]), .en(Write));  // open: Qn, preset, reset
  D_Flip_Flop d_ff_8 (.clk(CLK), .D(Data_In[7]), .Q(Data_Out[7]), .en(Write));  // open: Qn, preset, reset
  D_Flip_Flop d_ff_9 (.clk(CLK), .D(Data_In[8]), .Q(Data_Out[8]), .en(Write));  // open: Qn, preset, reset
  D_Flip_Flop d_ff_10 (.clk(CLK), .D(Data_In[9]), .Q(Data_Out[9]), .en(Write));  // open: Qn, preset, reset
  D_Flip_Flop d_ff_11 (.clk(CLK), .D(Data_In[10]), .Q(Data_Out[10]), .en(Write));  // open: Qn, preset, reset
  D_Flip_Flop d_ff_12 (.clk(CLK), .D(Data_In[11]), .Q(Data_Out[11]), .en(Write));  // open: Qn, preset, reset
  D_Flip_Flop d_ff_13 (.clk(CLK), .D(Data_In[12]), .Q(Data_Out[12]), .en(Write));  // open: Qn, preset, reset
  D_Flip_Flop d_ff_14 (.clk(CLK), .D(Data_In[13]), .Q(Data_Out[13]), .en(Write));  // open: Qn, preset, reset
  D_Flip_Flop d_ff_15 (.clk(CLK), .D(Data_In[14]), .Q(Data_Out[14]), .en(Write));  // open: Qn, preset, reset
  D_Flip_Flop d_ff_16 (.clk(CLK), .D(Data_In[15]), .Q(Data_Out[15]), .en(Write));  // open: Qn, preset, reset
endmodule

module Extender (
  input  [5:0] Imm,
  input  ExtOp,
  output [15:0] Out
);

  wire [15:0] bit_extender_1_out, bit_extender_2_out;

  assign bit_extender_1_out = {{10{1'b0}}, Imm};  // Bit_Extender bit_extender_1
  assign bit_extender_2_out = {{10{Imm[5]}}, Imm};  // Bit_Extender bit_extender_2
  Multiplexer #(.width(16)) multiplexer_1 (
    .in0(bit_extender_1_out), .in1(bit_extender_2_out), .out(Out), .sel(ExtOp));  // open: en
endmodule

module ALU (
  input  [15:0] A,
  input  [15:0] B,
  input  [2:0] ALU_Control,
  output [15:0] Result,
  output JR,
  output Zero
);

  wire comparator_1_lt;
  wire [15:0] adder_1_out, and_1_out, bit_extender_1_out, multiplexer_1_out, or_1_out, subtractor_1_out;

  Comparator #(.width(16)) comparator_1 (.a(A), .b(B), .lt(comparator_1_lt));  // open: gt, eq
  Subtractor #(.width(16)) subtractor_1 (.a(A), .b(B), .out(subtractor_1_out));  // open: bin, bout
  Adder #(.width(16)) adder_1 (.a(A), .b(B), .out(adder_1_out));  // open: cin, cout
  Multiplexer #(.width(16), .enable("false")) multiplexer_1 (
    .in0(A), .in1(B), .out(multiplexer_1_out), .sel(comparator_1_lt));
  assign or_1_out = A | B;  // OR_Gate or_1, 16 bits wide
  assign and_1_out = A & B;  // AND_Gate and_1, 16 bits wide
  assign bit_extender_1_out = {{15{1'b0}}, comparator_1_lt};  // Bit_Extender bit_extender_1
  Multiplexer #(.select(3), .width(16), .enable("false")) multiplexer_2 (
    .in0(A), .in1(bit_extender_1_out), .in2(subtractor_1_out), .in3(adder_1_out), .in4(adder_1_out),
    .in5(multiplexer_1_out), .in6(or_1_out), .in7(and_1_out), .out(Result), .sel(ALU_Control));
  and and_2 (JR, ~ALU_Control[0], ~ALU_Control[1], ~ALU_Control[2]);  // AND_Gate
  nor nor_1 (Zero, Result[0], Result[1], Result[2], Result[3], Result[4], Result[5], Result[6], Result[7], Result[8], Result[9], Result[10], Result[11], Result[12], Result[13], Result[14], Result[15]);
endmodule

module Alu_Control (
  input  [2:0] Main_Control,
  input  [2:0] Function,
  input  Type,
  output [2:0] ALU_Control,
  output Lws
);

  Multiplexer #(.width(3), .enable("false")) multiplexer_1 (
    .in0(Main_Control), .in1(Function), .out(ALU_Control), .sel(Type));
  and and_1 (Lws, ~ALU_Control[0], ~ALU_Control[1], ALU_Control[2]);  // AND_Gate
endmodule

module Control_Unit (
  input  [3:0] Opcode,
  output Jal,
  output Jump,
  output RegDest,
  output BEQ,
  output MemWrite,
  output MemRead,
  output MemToReg,
  output RegWrite,
  output MemByte,
  output lbu,
  output ALUSrc,
  output ExtOp,
  output R_Type,
  output [2:0] ALUOp
);

  wire ADDI_out, ANDI_out, J_out, Lb_out, LW_out, or_1_out, ORI_out, Sb_out, SW_out;

  and u_R_type (R_Type, ~Opcode[3], ~Opcode[2], ~Opcode[1], ~Opcode[0]);  // AND_Gate
  and LW (LW_out, ~Opcode[3], Opcode[2], ~Opcode[1], ~Opcode[0]);  // AND_Gate
  and SW (SW_out, ~Opcode[3], Opcode[2], Opcode[1], Opcode[0]);  // AND_Gate
  or or_1 (or_1_out, LW_out, SW_out, lbu, Lb_out, ADDI_out, Sb_out);
  and u_BEQ (BEQ, Opcode[3], ~Opcode[2], ~Opcode[1], Opcode[0]);  // AND_Gate
  and ADDI (ADDI_out, ~Opcode[3], ~Opcode[2], Opcode[1], Opcode[0]);  // AND_Gate
  and u_Lbu (lbu, ~Opcode[3], Opcode[2], ~Opcode[1], Opcode[0]);  // AND_Gate
  and ANDI (ANDI_out, ~Opcode[3], ~Opcode[2], ~Opcode[1], Opcode[0]);  // AND_Gate
  and ORI (ORI_out, ~Opcode[3], ~Opcode[2], Opcode[1], ~Opcode[0]);  // AND_Gate
  and Lb (Lb_out, ~Opcode[3], Opcode[2], Opcode[1], ~Opcode[0]);  // AND_Gate
  and J (J_out, Opcode[3], ~Opcode[2], Opcode[1], ~Opcode[0]);  // AND_Gate
  Priority_Encoder priority_encoder_1 (
    .in2(BEQ), .in3(or_1_out), .in6(ORI_out), .in7(ANDI_out), .out(ALUOp));  // open: in0, in1, in4, in5, en_in, gs, en_out
  and Sb (Sb_out, Opcode[3], ~Opcode[2], ~Opcode[1], ~Opcode[0]);  // AND_Gate
  and u_JAL (Jal, Opcode[3], ~Opcode[2], Opcode[1], Opcode[0]);  // AND_Gate
  or or_2 (Jump, Jal, J_out);
  or or_3 (MemWrite, SW_out, Sb_out);
  or or_4 (MemRead, LW_out, Lb_out, lbu);
  nor nor_1 (RegWrite, J_out, Sb_out, Jal, BEQ, SW_out);
  or or_5 (MemByte, Sb_out, Lb_out, lbu);
  nor nor_2 (ALUSrc, R_Type, BEQ);
  nor nor_3 (ExtOp, ORI_out, ANDI_out);

  assign MemToReg = MemRead;
  assign RegDest = R_Type;
endmodule

module PC_Control (
  input  Jump,
  input  BEQ,
  input  Zero,
  input  JR,
  input  [2:0] Rs,
  output [1:0] PC
);

  wire and_2_out, and_3_out;
  wire [1:1] and_1_out;

  and and_1 (and_1_out[1], BEQ, Zero);
  Multiplexer #(.width(2), .enable("false")) multiplexer_1 (
    .in0({and_1_out[1], Jump}), .in1(2'b11), .out(PC), .sel(and_2_out));
  and and_2 (and_2_out, ~and_3_out, JR);  // AND_Gate
  and and_3 (and_3_out, ~Rs[2], ~Rs[1], ~Rs[0]);  // AND_Gate
endmodule

module IF_buffer (
  input  [15:0] PC_iin,
  input  [15:0] IR_in,
  input  CLK,
  output [15:0] PC_out,
  output [15:0] IR_out
);

  Register #(.width(16)) register_1 (.D(PC_iin), .Q(PC_out), .clk(CLK));  // open: en, clr
  Register #(.width(16)) register_2 (.D(IR_in), .Q(IR_out), .clk(CLK));  // open: en, clr
endmodule

module ID_buffer (
  input  [15:0] in_1,
  input  [2:0] in_2,
  input  [2:0] in_3,
  input  [2:0] in_4,
  input  [15:0] in_5,
  input  [5:0] in_6,
  input  [15:0] in_7,
  input  [15:0] in_8,
  input  [2:0] in_9,
  input  in_10,
  input  in_11,
  input  in_12,
  input  in_13,
  input  in_14,
  input  in_15,
  input  in_16,
  input  in_17,
  input  in_18,
  input  in_19,
  input  in_20,
  input  in_21,
  input  CLK,
  output [15:0] out_23,
  output [2:0] out_24,
  output [2:0] out_25,
  output [2:0] out_26,
  output [15:0] out_27,
  output [5:0] out_28,
  output [15:0] out_29,
  output [15:0] out_30,
  output [2:0] out_31,
  output out_32,
  output out_33,
  output out_34,
  output out_35,
  output out_36,
  output out_37,
  output out_38,
  output out_39,
  output out_40,
  output out_41,
  output out_42,
  output out_43
);

  Register #(.width(16)) register_1 (.D(in_1), .Q(out_23), .clk(CLK));  // open: en, clr
  Register #(.width(3)) register_2 (.D(in_2), .Q(out_24), .clk(CLK));  // open: en, clr
  Register #(.width(3)) register_3 (.D(in_3), .Q(out_25), .clk(CLK));  // open: en, clr
  Register #(.width(3)) register_4 (.D(in_4), .Q(out_26), .clk(CLK));  // open: en, clr
  Register #(.width(16)) register_5 (.D(in_5), .Q(out_27), .clk(CLK));  // open: en, clr
  Register #(.width(6)) register_6 (.D(in_6), .Q(out_28), .clk(CLK));  // open: en, clr
  Register #(.width(16)) register_7 (.D(in_7), .Q(out_29), .clk(CLK));  // open: en, clr
  Register #(.width(16)) register_8 (.D(in_8), .Q(out_30), .clk(CLK));  // open: en, clr
  Register #(.width(3)) register_9 (.D(in_9), .Q(out_31), .clk(CLK));  // open: en, clr
  Register #(.width(1)) register_10 (.D(in_10), .Q(out_32), .clk(CLK));  // open: en, clr
  Register #(.width(1)) register_11 (.D(in_11), .Q(out_33), .clk(CLK));  // open: en, clr
  Register #(.width(1)) register_12 (.D(in_12), .Q(out_34), .clk(CLK));  // open: en, clr
  Register #(.width(1)) register_13 (.D(in_13), .Q(out_35), .clk(CLK));  // open: en, clr
  Register #(.width(1)) register_14 (.D(in_14), .Q(out_36), .clk(CLK));  // open: en, clr
  Register #(.width(1)) register_15 (.D(in_15), .Q(out_37), .clk(CLK));  // open: en, clr
  Register #(.width(1)) register_16 (.D(in_16), .Q(out_38), .clk(CLK));  // open: en, clr
  Register #(.width(1)) register_17 (.D(in_17), .Q(out_39), .clk(CLK));  // open: en, clr
  Register #(.width(1)) register_18 (.D(in_18), .Q(out_40), .clk(CLK));  // open: en, clr
  Register #(.width(1)) register_19 (.D(in_19), .Q(out_41), .clk(CLK));  // open: en, clr
  Register #(.width(1)) register_20 (.D(in_20), .Q(out_42), .clk(CLK));  // open: en, clr
  Register #(.width(1)) register_21 (.D(in_21), .Q(out_43), .clk(CLK));  // open: en, clr
endmodule

module EX_buffer (
  input  [2:0] in_1,
  input  [15:0] in_2,
  input  [15:0] in_3,
  input  in_4,
  input  in_5,
  input  in_6,
  input  in_7,
  input  in_8,
  input  in_9,
  input  CLK,
  output [2:0] out_11,
  output [15:0] out_12,
  output [15:0] out_13,
  output out_14,
  output out_15,
  output out_16,
  output out_17,
  output out_18,
  output out_19
);

  Register #(.width(3)) register_1 (.D(in_1), .Q(out_11), .clk(CLK));  // open: en, clr
  Register #(.width(16)) register_2 (.D(in_2), .Q(out_12), .clk(CLK));  // open: en, clr
  Register #(.width(16)) register_3 (.D(in_3), .Q(out_13), .clk(CLK));  // open: en, clr
  Register #(.width(1)) register_4 (.D(in_4), .Q(out_14), .clk(CLK));  // open: en, clr
  Register #(.width(1)) register_5 (.D(in_5), .Q(out_15), .clk(CLK));  // open: en, clr
  Register #(.width(1)) register_6 (.D(in_6), .Q(out_16), .clk(CLK));  // open: en, clr
  Register #(.width(1)) register_7 (.D(in_7), .Q(out_17), .clk(CLK));  // open: en, clr
  Register #(.width(1)) register_8 (.D(in_8), .Q(out_18), .clk(CLK));  // open: en, clr
  Register #(.width(1)) register_9 (.D(in_9), .Q(out_19), .clk(CLK));  // open: en, clr
endmodule

module MEM_buffer (
  input  [2:0] in_1,
  input  [15:0] in_2,
  input  [15:0] in_3,
  input  in_4,
  input  in_5,
  input  CLK,
  output [2:0] out_7,
  output [15:0] out_8,
  output [15:0] out_9,
  output out_10,
  output out_11
);

  Register #(.width(3)) register_1 (.D(in_1), .Q(out_7), .clk(CLK));  // open: en, clr
  Register #(.width(16)) register_2 (.D(in_2), .Q(out_8), .clk(CLK));  // open: en, clr
  Register #(.width(16)) register_3 (.D(in_3), .Q(out_9), .clk(CLK));  // open: en, clr
  Register #(.width(1)) register_4 (.D(in_4), .Q(out_10), .clk(CLK));  // open: en, clr
  Register #(.width(1)) register_5 (.D(in_5), .Q(out_11), .clk(CLK));  // open: en, clr
endmodule

module Forward (
  input  [2:0] RS,
  input  [2:0] Rd_mem,
  input  [2:0] RT,
  input  [2:0] Rd_wb,
  input  RegWrite_mem,
  input  RegWrite_WB,
  output [1:0] ForwardA,
  output [1:0] ForwardB
);

  wire comparator_1_eq, comparator_2_eq, comparator_3_eq, comparator_4_eq, comparator_5_eq, comparator_6_eq,
       comparator_7_eq, comparator_8_eq, comparator_9_eq, not_1_out, not_2_out, not_3_out, not_4_out,
       not_5_out;
  wire [0:0] and_3_out, and_4_out;
  wire [1:1] and_1_out, and_2_out;

  assign ForwardA = {and_1_out[1], 1'b0} | {1'b0, and_3_out[0]};  // OR_Gate or_1, 2 bits wide
  assign ForwardB = {and_2_out[1], 1'b0} | {1'b0, and_4_out[0]};  // OR_Gate or_2, 2 bits wide
  and and_1 (and_1_out[1], RegWrite_mem, not_1_out, comparator_7_eq);
  and and_2 (and_2_out[1], RegWrite_mem, not_2_out, comparator_9_eq);
  not not_1 (not_1_out, comparator_6_eq);
  not not_2 (not_2_out, comparator_8_eq);
  and and_3 (and_3_out[0], RegWrite_WB, not_3_out, not_4_out, comparator_3_eq);
  Comparator #(.width(3)) comparator_1 (.a(3'b000), .b(Rd_wb), .eq(comparator_1_eq));  // open: gt, lt
  Comparator #(.width(3)) comparator_2 (.a(Rd_mem), .b(RS), .eq(comparator_2_eq));  // open: gt, lt
  Comparator #(.width(3)) comparator_3 (.a(Rd_wb), .b(RS), .eq(comparator_3_eq));  // open: gt, lt
  and and_4 (and_4_out[0], RegWrite_WB, comparator_1_eq, not_5_out, comparator_5_eq);
  Comparator #(.width(3)) comparator_4 (.a(Rd_mem), .b(RT), .eq(comparator_4_eq));  // open: gt, lt
  Comparator #(.width(3)) comparator_5 (.a(Rd_wb), .b(RT), .eq(comparator_5_eq));  // open: gt, lt
  Comparator #(.width(3)) comparator_6 (.a(3'b000), .b(Rd_mem), .eq(comparator_6_eq));  // open: gt, lt
  Comparator #(.width(3)) comparator_7 (.a(RS), .b(Rd_mem), .eq(comparator_7_eq));  // open: gt, lt
  Comparator #(.width(3)) comparator_8 (.a(3'b000), .b(Rd_mem), .eq(comparator_8_eq));  // open: gt, lt
  Comparator #(.width(3)) comparator_9 (.a(RT), .b(Rd_mem), .eq(comparator_9_eq));  // open: gt, lt
  not not_3 (not_3_out, comparator_1_eq);
  not not_4 (not_4_out, comparator_2_eq);
  not not_5 (not_5_out, comparator_4_eq);
endmodule

module byte_Extender (
  input  [15:0] Imm,
  input  lbu,
  output [15:0] Out
);

  wire [15:0] bit_extender_1_out, bit_extender_2_out;

  assign bit_extender_1_out = {{8{Imm[7]}}, Imm[7:0]};  // Bit_Extender bit_extender_1
  assign bit_extender_2_out = {{8{1'b0}}, Imm[7:0]};  // Bit_Extender bit_extender_2
  Multiplexer #(.width(16), .enable("false")) multiplexer_1 (
    .in0(bit_extender_1_out), .in1(bit_extender_2_out), .out(Out), .sel(lbu));
endmodule
